# Fritzing sketch SparkShield_RGB_LedStrip_Driver - N-Channel MOSFET (saved by Fritzing 0.9.0b)
circuit board: 6.71053cm x 2.68358cm
breadboards: 1

parts:
  Part1 = Spark Core (v1.0)
  Q4 = Basic FET N-Channel [package="TO220 [THT]"]
  Q5 = Basic FET N-Channel [package="TO220 [THT]"]
  Q6 = Basic FET N-Channel [package="TO220 [THT]"]
  Power_plug1 = Power plug
  J1 = female pin header, 2 pins [form="♀ (female)"]
  J2 = female pin header, 2 pins [form="♀ (female)"]
  C5 = Capacitor [package=cap-pth-small]
  C6 = Capacitor [package=cap-pth-small]
  U1 = Voltage Regulator - 5V [package="DPak [SMD]"]
  IR1 = TSOP312.., 314.. [package=THT]

nets:
  N1: Part1.A0, Q6.gate
  N2: Part1.A1, Q5.gate
  N3: Part1.A6, Q4.gate
  GND: Part1.GND, Q4.source, Q5.source, Q6.source, Power_plug1.GND, C5.2, C6.1, U1.GND, IR1.GND
  N4: Part1.VIN, C5.1, U1.output_voltage, IR1.Vs
  N5: Part1.D2, IR1.Data
  N6: Q4.drain, J1.pin1
  N7: Q5.drain, J2.pin2
  N8: Q6.drain, J2.pin1
  N9: Power_plug1.VCC, J1.pin2, C6.2, U1.input_voltage
