# Fritzing sketch SparkShield_RGB_LedStrip_Driver - NPN (saved by Fritzing 0.9.0b)
circuit board: 7.32448cm x 2.99283cm
breadboards: 1

parts:
  Part1 = Spark Core (v1.0)
  R1 = Resistor [tolerance=±5% resistance=220 package=THT]
  Power_plug1 = Power plug
  R2 = Resistor [tolerance=±5% resistance=220 package=THT]
  R3 = Resistor [tolerance=±5% resistance=220 package=THT]
  J1 = female pin header, 2 pins [form="♀ (female)"]
  J2 = female pin header, 2 pins [form="♀ (female)"]
  Q7 = npn-Powertransistor [package="TO220 [THT]"]
  Q8 = npn-Powertransistor [package="TO220 [THT]"]
  Q9 = npn-Powertransistor [package="TO220 [THT]"]

nets:
  N1: Part1.A0, R1.Pin_0
  N2: Part1.A1, R2.Pin_0
  N3: Part1.A6, R3.Pin_0
  GND: Part1.GND, Power_plug1.GND, Q7.emitter, Q8.emitter, Q9.emitter
  VIN: Part1.VIN, Power_plug1.VCC
  N4: R1.Pin_1, Q7.base
  N5: R2.Pin_1, Q8.base
  N6: R3.Pin_1, Q9.base
  N7: J1.pin1, Q9.collector
  N8: J2.pin1, Q7.collector
  N9: J2.pin2, Q8.collector
